# Fritzing sketch TTGO-T-BEAM-RC522 (saved by Fritzing 0.9.10b)
breadboards: 1

parts:
  Part1 = RFID-RC522-v2
  M1 = TTGO T-Beam V1.1

nets:
  N1: Part1.SDA, M1.2
  N2: Part1.SCK, M1.14
  N3: Part1.MOSI, M1.13
  N4: Part1.MISO, M1.4
  GND: Part1.GND, M1.GND
  N5: Part1.RST, M1.33
  3.3V: Part1.3.3V, M1.3V3

notes:
  Pinouts of T-BEAM to RC522
  RST: 33
  CS/SS: 2
  MISO: 4
  MOSI: 13
  SCK: 14

custom parts:
  RFID-RC522-v2: A simple China made RFID-RC522 Reader; do check the pin labels, as this is a MFRC522 based clone.
  TTGO T-Beam V1.1: LILYGO® TTGO Meshtastic T-Beam V1.1 ESP32 433/868/915/923Mhz WiFi Bluetooth ESP32 GPS NEO-6M SMA 18650 Battery Holder With OLED
